# Fritzing sketch schematic (saved by Fritzing 0.9.3b)
breadboards: 1

parts:
  Raspberry_Pi_1 = Raspberry Pi 2
  R1 = Resistor [tolerance=±5% resistance=300 package=THT]
  LED = LED - 5mm [color="Red (633nm)" package="5 mm [THT]"]
  SPKR1 = Loudspeaker
  J1 = Basic Servo
  R2 = Resistor [tolerance=±5% resistance=10k package=THT]
  S1 = Pushbutton [package=THT]

nets:
  N1: Raspberry_Pi_1.GPIO17, LED.anode
  N2: Raspberry_Pi_1.GPIO19, SPKR1.pin1
  GND: Raspberry_Pi_1.GND, R1.Pin_1, SPKR1.pin2, J1.gnd, S1.leg0
  N3: Raspberry_Pi_1.GPIO23, S1.leg1
  N4: Raspberry_Pi_1.GPIO18, R2.Pin_0
  N5: Raspberry_Pi_1.5V, J1.pulse
  N6: R1.Pin_0, LED.cathode
  N7: J1.vcc, R2.Pin_1
